// Digital circuit dig_clock.dig as structural Verilog
module dig_clock (
  input  clk
);

  wire button_1_out, button_2_out, button_3_out, decoder_1_out_0, decoder_1_out_1, decoder_1_out_2,
       dipswitch_1_out, u_clockDivider_new_clk, u_fsm_clock_set_output, u_fsm_decrement_output,
       u_fsm_increment_output;
  wire [1:0] u_fsm_changed;
  wire [3:0] u_binaryToBCD_2_tens, u_binaryToBCD_2_units, u_binaryToBCD_3_tens, u_binaryToBCD_3_units,
       u_binaryToBCD_tens, u_binaryToBCD_units;
  wire [4:0] u_minCounter_hours;
  wire [5:0] u_minCounter_mins, u_minCounter_secs;
  wire [6:0] u_clockDisplay_2_pins, u_clockDisplay_3_pins, u_clockDisplay_4_pins, u_clockDisplay_5_pins,
       u_clockDisplay_6_pins, u_clockDisplay_pins;

  DipSwitch dipswitch_1 (.out(dipswitch_1_out));
  Button button_1 (.out(button_1_out));
  Button button_2 (.out(button_2_out));
  Button button_3 (.out(button_3_out));
  fsm #(.applicationType("IVERILOG"), .iverilogOptions("-g2012"), .CodeFile("/Users/ameerassi/VsCode/DigitalClock/fsm.sv")) u_fsm (
    .clk(clk), .rst(dipswitch_1_out), .clock_set(button_1_out), .increment(button_2_out),
    .decrement(button_3_out), .clock_set_output(u_fsm_clock_set_output),
    .increment_output(u_fsm_increment_output), .decrement_output(u_fsm_decrement_output),
    .changeD(u_fsm_changed));
  clockDivider #(.applicationType("IVERILOG"), .iverilogOptions("-g2012"), .CodeFile("/Users/ameerassi/VsCode/DigitalClock/clockDivider.sv")) u_clockDivider (
    .clk(clk), .rst(dipswitch_1_out), .new_clk(u_clockDivider_new_clk));
  minCounter #(.applicationType("IVERILOG"), .iverilogOptions("-g2012"), .CodeFile("/Users/ameerassi/VsCode/DigitalClock/minCounter.sv")) u_minCounter (
    .clk(clk), .rst(dipswitch_1_out), .tick(u_clockDivider_new_clk), .clock_set(u_fsm_clock_set_output),
    .increment(u_fsm_increment_output), .decrement(u_fsm_decrement_output), .changeD(u_fsm_changed),
    .mins(u_minCounter_mins), .secs(u_minCounter_secs), .hours(u_minCounter_hours));
  Decoder #(.Selector_Bits(2)) decoder_1 (
    .sel(u_fsm_changed), .out_0(decoder_1_out_0), .out_1(decoder_1_out_1), .out_2(decoder_1_out_2));  // open: out_3
  binaryToBCD #(.applicationType("IVERILOG"), .iverilogOptions("-g2012"), .CodeFile("/Users/ameerassi/VsCode/DigitalClock/binaryToBCD.sv")) u_binaryToBCD (
    .number(u_minCounter_mins), .units(u_binaryToBCD_units), .tens(u_binaryToBCD_tens));
  binaryToBCD #(.applicationType("IVERILOG"), .iverilogOptions("-g2012"), .CodeFile("/Users/ameerassi/VsCode/DigitalClock/binaryToBCD.sv")) u_binaryToBCD_2 (
    .number(u_minCounter_secs), .units(u_binaryToBCD_2_units), .tens(u_binaryToBCD_2_tens));
  binaryToBCD #(.applicationType("IVERILOG"), .iverilogOptions("-g2012"), .CodeFile("/Users/ameerassi/VsCode/DigitalClock/binaryToBCD.sv")) u_binaryToBCD_3 (
    .number({1'b0, u_minCounter_hours}), .units(u_binaryToBCD_3_units), .tens(u_binaryToBCD_3_tens));
  clockDisplay #(.applicationType("IVERILOG"), .iverilogOptions("-g2012"), .CodeFile("/Users/ameerassi/VsCode/DigitalClock/clockDisplay.sv")) u_clockDisplay (
    .num(u_binaryToBCD_2_tens), .blink(decoder_1_out_0), .tick(u_clockDivider_new_clk),
    .pins(u_clockDisplay_pins));
  clockDisplay #(.applicationType("IVERILOG"), .iverilogOptions("-g2012"), .CodeFile("/Users/ameerassi/VsCode/DigitalClock/clockDisplay.sv")) u_clockDisplay_2 (
    .num(u_binaryToBCD_2_units), .blink(decoder_1_out_0), .tick(u_clockDivider_new_clk),
    .pins(u_clockDisplay_2_pins));
  clockDisplay #(.applicationType("IVERILOG"), .iverilogOptions("-g2012"), .CodeFile("/Users/ameerassi/VsCode/DigitalClock/clockDisplay.sv")) u_clockDisplay_3 (
    .num(u_binaryToBCD_tens), .blink(decoder_1_out_1), .tick(u_clockDivider_new_clk),
    .pins(u_clockDisplay_3_pins));
  clockDisplay #(.applicationType("IVERILOG"), .iverilogOptions("-g2012"), .CodeFile("/Users/ameerassi/VsCode/DigitalClock/clockDisplay.sv")) u_clockDisplay_4 (
    .num(u_binaryToBCD_units), .blink(decoder_1_out_1), .tick(u_clockDivider_new_clk),
    .pins(u_clockDisplay_4_pins));
  clockDisplay #(.applicationType("IVERILOG"), .iverilogOptions("-g2012"), .CodeFile("/Users/ameerassi/VsCode/DigitalClock/clockDisplay.sv")) u_clockDisplay_5 (
    .num(u_binaryToBCD_3_tens), .blink(decoder_1_out_2), .tick(u_clockDivider_new_clk),
    .pins(u_clockDisplay_5_pins));
  clockDisplay #(.applicationType("IVERILOG"), .iverilogOptions("-g2012"), .CodeFile("/Users/ameerassi/VsCode/DigitalClock/clockDisplay.sv")) u_clockDisplay_6 (
    .num(u_binaryToBCD_3_units), .blink(decoder_1_out_2), .tick(u_clockDivider_new_clk),
    .pins(u_clockDisplay_6_pins));
  Seven_Seg seven_seg_1 (
    .a(u_clockDisplay_pins[0]), .b(u_clockDisplay_pins[1]), .c(u_clockDisplay_pins[2]),
    .d(u_clockDisplay_pins[3]), .e(u_clockDisplay_pins[4]), .f(u_clockDisplay_pins[5]),
    .g(u_clockDisplay_pins[6]), .dp(u_clockDisplay_pins[6]));
  Seven_Seg seven_seg_2 (
    .a(u_clockDisplay_3_pins[0]), .b(u_clockDisplay_3_pins[1]), .c(u_clockDisplay_3_pins[2]),
    .d(u_clockDisplay_3_pins[3]), .e(u_clockDisplay_3_pins[4]), .f(u_clockDisplay_3_pins[5]),
    .g(u_clockDisplay_3_pins[6]), .dp(u_clockDisplay_3_pins[6]));
  Seven_Seg seven_seg_3 (
    .a(u_clockDisplay_5_pins[0]), .b(u_clockDisplay_5_pins[1]), .c(u_clockDisplay_5_pins[2]),
    .d(u_clockDisplay_5_pins[3]), .e(u_clockDisplay_5_pins[4]), .f(u_clockDisplay_5_pins[5]),
    .g(u_clockDisplay_5_pins[6]), .dp(u_clockDisplay_5_pins[6]));
  Seven_Seg seven_seg_4 (
    .a(u_clockDisplay_2_pins[0]), .b(u_clockDisplay_2_pins[1]), .c(u_clockDisplay_2_pins[2]),
    .d(u_clockDisplay_2_pins[3]), .e(u_clockDisplay_2_pins[4]), .f(u_clockDisplay_2_pins[5]),
    .g(u_clockDisplay_2_pins[6]), .dp(u_clockDisplay_2_pins[6]));
  Seven_Seg seven_seg_5 (
    .a(u_clockDisplay_4_pins[0]), .b(u_clockDisplay_4_pins[1]), .c(u_clockDisplay_4_pins[2]),
    .d(u_clockDisplay_4_pins[3]), .e(u_clockDisplay_4_pins[4]), .f(u_clockDisplay_4_pins[5]),
    .g(u_clockDisplay_4_pins[6]), .dp(u_clockDisplay_4_pins[6]));
  Seven_Seg seven_seg_6 (
    .a(u_clockDisplay_6_pins[0]), .b(u_clockDisplay_6_pins[1]), .c(u_clockDisplay_6_pins[2]),
    .d(u_clockDisplay_6_pins[3]), .e(u_clockDisplay_6_pins[4]), .f(u_clockDisplay_6_pins[5]),
    .g(u_clockDisplay_6_pins[6]), .dp(u_clockDisplay_6_pins[6]));

  // Notes on the sheet:
  //   clk: Hz: 10
endmodule
